# Fritzing sketch Arduino_Uno_Schema (saved by Fritzing 0.9.2b)
breadboards: 1

parts:
  Arduino_Uno = Arduino Uno (Rev3)
  Fotoresistenza = PHOTOCELL [package=photocell-kit]
  part = Resistor [tolerance=±5% resistance=10k package="2010 [SMD]"]
  Schermo_LCD = LCD screen
  part_2 = Resistor [tolerance=±5% resistance=220 package="0603 [SMD]"]
  LED2 = LEDs [package=led10mm]
  Led_Giardino = LEDs [package=led10mm]
  Led_Sala3 = LEDs [package=led10mm]
  R7 = Resistor [tolerance=±5% resistance=220 package="2512 [SMD]"]
  part_3 = Resistor [tolerance=±5% resistance=220 package="2512 [SMD]"]
  Arduino_Yun = Resistor [tolerance=±5% resistance=220 package="2512 [SMD]"]
  Transistor_Npn = TRANSISTOR_NPN [package=to-92-ammo]
  Allarme = Piezo Speaker

nets:
  N1: Arduino_Uno.A0, Fotoresistenza.P$2, part.Pin_0
  N2: Arduino_Uno.D10_PWM/SS, Schermo_LCD.V0
  N3: Arduino_Uno.D11_PWM/MOSI, Schermo_LCD.E
  N4: Arduino_Uno.D12/MISO, Schermo_LCD.RS
  N5: Arduino_Uno.D13/SCK, Transistor_Npn.B
  GND: Arduino_Uno.GND, part.Pin_1, Schermo_LCD.VSS, Schermo_LCD.R/W, Schermo_LCD.LED-, Transistor_Npn.E, Allarme.pin2
  N6: Arduino_Uno.D3_PWM, Schermo_LCD.DB7
  N7: Arduino_Uno.D4, Schermo_LCD.DB6
  N8: Arduino_Uno.D5_PWM, Schermo_LCD.DB5
  N9: Arduino_Uno.D6_PWM, Schermo_LCD.DB4
  N10: Arduino_Uno.D7, Allarme.pin1
  5V: Arduino_Uno.5V, Fotoresistenza.P$1, Schermo_LCD.VDD, part_2.Pin_0, Led_Giardino.A, Led_Sala3.A
  N11: Schermo_LCD.LED+, part_2.Pin_1
  N12: LED2.C, Arduino_Yun.Pin_1
  N13: Led_Giardino.C, R7.Pin_1
  N14: Led_Sala3.C, part_3.Pin_0
  N15: R7.Pin_0, part_3.Pin_1, Arduino_Yun.Pin_0, Transistor_Npn.C
