# Fritzing sketch Arduino_Yun_Schema (saved by Fritzing 0.9.2b)
breadboards: 1

parts:
  Arduino_Yun = Arduino Yun
  Temperatura = TMP36 [package=to-92-kit]
  Ventola = DC Motor
  Servo_Box = Basic Servo
  Servo_Cancello = Basic Servo
  100_uF = Capacitor Polarized [package=cpol-radial-100uf-25v]
  Sensori_Finestre = Reed switch [package=THT]
  part = Resistor [tolerance=±5% resistance=220 package="2512 [SMD]"]
  part_2 = Resistor [tolerance=±5% resistance=220 package="2512 [SMD]"]
  part_3 = LEDs [package=led10mm]
  RGB_Camera = RGB LED (com. cathode, rbg) [package="5 mm [THT]"]
  100_uF_2 = Capacitor Polarized [package=cpol-radial-100uf-25v]
  Transistor_Npn = TRANSISTOR_NPN [package=to-92-ammo]
  Arduino_Uno = Resistor [tolerance=±5% resistance=220 package="2512 [SMD]"]
  part_4 = Resistor [tolerance=±5% resistance=220 package="2512 [SMD]"]
  part_5 = Resistor [tolerance=±5% resistance=4.7k package="2010 [SMD]"]
  Led_Sala1 = LEDs [package=led10mm]
  part_6 = Resistor [tolerance=±5% resistance=220 package="2512 [SMD]"]
  Led_Sala = LEDs [package=led10mm]
  part_7 = Resistor [tolerance=±5% resistance=220 package="2512 [SMD]"]
  10_uF = Capacitor Polarized [package=cpol-radial-10uf-25v]
  Sensori_Finestre1 = Reed switch [package=THT]
  Sensori_Finestre2 = Reed switch [package=THT]

nets:
  N1: Arduino_Yun.A0, Temperatura.VOUT
  VCC: Arduino_Yun.5V, Temperatura.VCC, Servo_Cancello.vcc, part_3.A, 100_uF_2.+, part_5.Pin_1, Led_Sala1.A, Led_Sala.A
  GND: Arduino_Yun.GND, Temperatura.GND, Ventola.pin_2, Servo_Box.gnd, Servo_Cancello.gnd, 100_uF.-, RGB_Camera.common_cathode, 100_uF_2.-, Transistor_Npn.E, 10_uF.-, Sensori_Finestre2.pin_1
  N2: Arduino_Yun.D9_PWM, Servo_Cancello.pulse
  N3: Arduino_Yun.D10_PWM/SS, Servo_Box.pulse
  N4: Arduino_Yun.D2, Ventola.pin_1
  N5: Arduino_Yun.D3_PWM, part.Pin_0
  N6: Arduino_Yun.D4, Transistor_Npn.B
  N7: Arduino_Yun.D5_PWM, Arduino_Uno.Pin_0
  N8: Arduino_Yun.D6_PWM, part_2.Pin_0
  N9: Arduino_Yun.D7, Sensori_Finestre.pin_2, part_5.Pin_0, 10_uF.+
  N10: Servo_Box.vcc, 100_uF.+
  N11: Sensori_Finestre.pin_1, Sensori_Finestre1.pin_2
  N12: part.Pin_1, RGB_Camera.green_anode
  N13: part_2.Pin_1, RGB_Camera.red_anode
  N14: part_3.C, part_4.Pin_0
  N15: RGB_Camera.blue_anode, Arduino_Uno.Pin_1
  N16: Transistor_Npn.C, part_4.Pin_1, part_6.Pin_1, part_7.Pin_1
  N17: Led_Sala1.C, part_6.Pin_0
  N18: Led_Sala.C, part_7.Pin_0
  N19: Sensori_Finestre1.pin_1, Sensori_Finestre2.pin_2
